# Fritzing sketch vysilac (saved by Fritzing 0.9.4)
breadboards: 1

parts:
  433_MHz_vysílač = Mystery Part - 3 pins [chip_label=? package=THT]
  Napájecí_modul_pro_nepájivá_pole = Adjustable Breadboard Power Supply
  ESP32-S = ESP32S-HiLetgo [part_number=ESP32S-HiLetgo]

nets:
  N1: 433_MHz_vysílač.pin2, ESP32-S.GPIO23
  N2: 433_MHz_vysílač.pin3, Napájecí_modul_pro_nepájivá_pole.Vin-, ESP32-S.GND
  N3: Napájecí_modul_pro_nepájivá_pole.Vout+, ESP32-S.VIN

custom parts:
  Mystery Part - 3 pins: A dummy, proxy, ersatz, stand-in part for whatever you want. With 3 pins on a 100 mil inline pin header footprint.
  ESP32S-HiLetgo: HiLetgo ESP-WROOM-32 ESP32 ESP-32S Development Board 2.4GHz Dual-Mode WiFi + Bluetooth Dual Cores Microcontroller The ESP32 integrated with Antenna switches, RF Balun, power amplifiers, low-noise amplifiers, filters, and management modules, and the entire solution occupies the least area of PCB. 2.4 GHz Wi-Fi plus Bluetooth dual-mode chip, with TSMC Ultra-low power consumption 40nm technology,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
